// Logisim project Basic Logic Circuit.circ as structural Verilog: 1 circuit, main circuit main
module main (
  input  X,
  input  Z,
  input  Y,
  input  X_2,
  input  Z_2,
  input  Y_2,
  output out_7,
  output out_8
);

  wire and_1_out, and_2_out, and_3_out, and_4_out, and_6_out, and_7_out, not_1_out, not_2_out, not_3_out,
       or_1_out, or_2_out, or_3_out;

  not not_1 (not_1_out, Z);
  not not_2 (not_2_out, X);
  not not_3 (not_3_out, Z);
  or or_1 (or_1_out, X_2, Z_2);
  and and_1 (and_1_out, Y, Z);
  and and_2 (and_2_out, Y, not_1_out);
  and and_3 (and_3_out, not_2_out, Z);
  and and_4 (and_4_out, X, not_3_out);
  and and_5 (out_8, or_1_out, Y_2);
  or or_2 (or_2_out, and_1_out, and_2_out);
  or or_3 (or_3_out, and_3_out, and_4_out);
  and and_6 (and_6_out, X, or_2_out);
  and and_7 (and_7_out, or_3_out, Y);
  or or_4 (out_7, and_6_out, and_7_out);
endmodule
