// Logisim project buyFuction.circ as structural Verilog: 1 circuit, main circuit main
module main (
  input  Pain_Webster,
  input  Meg_A__Cash,
  input  Madame_Lazora,
  output out_4
);

  wire and_1_out;

  and and_1 (and_1_out, Pain_Webster, Meg_A__Cash);
  or or_1 (out_4, and_1_out, Madame_Lazora);
endmodule
